// Digital circuit JUMP_DECODER.dig as structural Verilog
module JUMP_DECODER (
  input  j2,
  input  j1,
  input  j0,
  input  ng,
  input  zr,
  output Y
);

  wire and_1_out, and_2_out, and_3_out, and_4_out, not_1_out, not_2_out, or_1_out;

  not not_1 (not_1_out, ng);
  not not_2 (not_2_out, zr);
  and and_1 (and_1_out, not_1_out, not_2_out);
  and and_2 (and_2_out, j1, zr);
  and and_3 (and_3_out, j2, ng);
  and and_4 (and_4_out, j0, and_1_out);
  or or_1 (or_1_out, and_2_out, and_3_out);
  or or_2 (Y, and_4_out, or_1_out);
endmodule
